# Fritzing sketch schematic (saved by Fritzing 0.9.3b)
breadboards: 1

parts:
  U1 = NodeMCU V1.0
  U2 = 74HC595 [package="DIP16 [THT]"]
  24V = AC Power [voltage=5 frequency=60]
  AD050030B1 = AD050030B5 [part_number=AD050030B5]
  8_Channel_Relay1 = 8 Channel Power Relay
  Zone_1_&_2 = Screw terminal - 2 pins [package=THT]
  Zone_5_&_6 = Screw terminal - 2 pins [package=THT]
  Zone_3_&_4 = Screw terminal - 2 pins [package=THT]
  Zone_7_&_8 = Screw terminal - 2 pins [package=THT]
  Common = Screw terminal - 2 pins [package=THT]

nets:
  Data: U1.D1, U2.DS
  Clock: U1.D2, U2.SH_CP
  3V3: U1.3V3, U2.MR, U2.VCC
  GND: U1.GND, U2.GND, U2.OE, AD050030B1.-Vo, 8_Channel_Relay1.GND
  Latch: U1.D5, U2.ST_CP
  5V: U1.Vin, AD050030B1.+Vo, 8_Channel_Relay1.JD-VCC
  Relay 2: U2.Q1, 8_Channel_Relay1.IN2
  Relay 3: U2.Q2, 8_Channel_Relay1.IN3
  Relay 4: U2.Q3, 8_Channel_Relay1.IN4
  Relay 5: U2.Q4, 8_Channel_Relay1.IN5
  Relay 6: U2.Q5, 8_Channel_Relay1.IN6
  Relay 7: U2.Q6, 8_Channel_Relay1.IN7
  Relay 8: U2.Q7, 8_Channel_Relay1.IN8
  Relay 1: U2.Q0, 8_Channel_Relay1.IN1
  N1: 24V.V+, AD050030B1.AC_1, Common.pin1, Common.pin2
  N2: 24V.V-, AD050030B1.AC_2, 8_Channel_Relay1.COM
  3.3V: 8_Channel_Relay1.VCC
  N3: 8_Channel_Relay1.NO#23, Zone_1_&_2.pin1
  N4: 8_Channel_Relay1.NO#26, Zone_1_&_2.pin2
  N5: 8_Channel_Relay1.NO#29, Zone_3_&_4.pin1
  N6: 8_Channel_Relay1.NO#32, Zone_3_&_4.pin2
  N7: 8_Channel_Relay1.NO#35, Zone_5_&_6.pin1
  N8: 8_Channel_Relay1.NO#38, Zone_5_&_6.pin2
  N9: 8_Channel_Relay1.NO#41, Zone_7_&_8.pin1
  N10: 8_Channel_Relay1.NO#44, Zone_7_&_8.pin2

custom parts:
  NodeMCU V1.0: ESP8266 based NodeMCU
  AD050030B5: AC-DC 220V to 12V Step-Down Power Supply Module forked from Iyad Nahas
  8 Channel Power Relay: An 8 channel power relay. The module operates at 5V.
